// Logisim project 1-Bit ALU.circ as structural Verilog: 1 circuit, main circuit main
module main (
  input  A0,
  input  B0,
  input  A0_2,
  input  B0_2,
  input  A0_3,
  input  B0_3,
  input  [1:0] S1_S0,
  input  A0_4,
  input  B0_4,
  input  C0,
  output F0,
  output Carry
);

  wire adder_1_out, AND_out, NOR_out, XOR_out;

  and AND (AND_out, A0, B0);
  nor NOR (NOR_out, A0_2, B0_2);
  xor XOR (XOR_out, A0_3, B0_3);
  Adder #(.width(1)) adder_1 (.a(B0_4), .b(C0), .out(adder_1_out), .cin(A0_4), .cout(Carry));
  Multiplexer #(.select(2), .enable("false")) multiplexer_1 (
    .in0(AND_out), .in1(NOR_out), .in2(XOR_out), .in3(adder_1_out), .out(F0), .sel(S1_S0));

  // Notes on the sheet:
  //   Full Adder
endmodule
