// Logisim project 3-bit-Asynchronous_down_counter.circ as structural Verilog: 1 circuit, main circuit main
module main (
  input  High,
  input  Constant,
  input  in_3,
  output Q0,
  output Q1,
  output Q2
);

  wire CLK_out, IC7476_2_qn, IC7476_qn;

  Clock CLK (.out(CLK_out));
  J_K_Flip_Flop #(.trigger("falling")) IC7476 (
    .J(High), .clk(CLK_out), .K(High), .Q(Q0), .Qn(IC7476_qn), .preset(in_3), .reset(in_3));  // open: en
  J_K_Flip_Flop #(.trigger("falling")) IC7476_2 (
    .J(High), .clk(IC7476_qn), .K(High), .Q(Q1), .Qn(IC7476_2_qn), .preset(in_3), .reset(in_3));  // open: en
  J_K_Flip_Flop #(.trigger("falling")) IC7476_3 (
    .J(High), .clk(IC7476_2_qn), .K(High), .Q(Q2), .preset(in_3), .reset(in_3));  // open: Qn, en
  Hex_Digit_Display hex_digit_display_1 (.value({Constant, Q2, Q1, Q0}));  // open: dp
endmodule
