// Logisim project 3-bit-Synchronous_down_counter.circ as structural Verilog: 1 circuit, main circuit main
module main (
  input  High,
  input  Constant,
  input  Present,
  input  Clear,
  output Q0,
  output Q1,
  output Q2
);

  wire and_1_out, CLK_out, IC7476_2_qn, IC7476_qn;

  Clock CLK (.out(CLK_out));
  J_K_Flip_Flop #(.trigger("falling")) IC7476 (
    .J(High), .clk(CLK_out), .K(High), .Q(Q0), .Qn(IC7476_qn), .preset(Present), .reset(Clear));  // open: en
  J_K_Flip_Flop #(.trigger("falling")) IC7476_2 (
    .J(IC7476_qn), .clk(CLK_out), .K(IC7476_qn), .Q(Q1), .Qn(IC7476_2_qn), .preset(Present), .reset(Clear));  // open: en
  and and_1 (and_1_out, IC7476_qn, IC7476_2_qn);
  J_K_Flip_Flop #(.trigger("falling")) IC7476_3 (
    .J(and_1_out), .clk(CLK_out), .K(and_1_out), .Q(Q2), .preset(Present), .reset(Clear));  // open: Qn, en
  Hex_Digit_Display hex_digit_display_1 (.value({Constant, Q2, Q1, Q0}));  // open: dp
endmodule
