// Logisim project 3-bit-Synchronous_up_counter.circ as structural Verilog: 1 circuit, main circuit main
module main (
  input  High,
  input  Constant,
  input  Present,
  input  Clear,
  output Q0,
  output Q1,
  output Q2
);

  wire AND_out, CLK_out;

  Clock CLK (.out(CLK_out));
  J_K_Flip_Flop #(.trigger("falling")) IC7476 (
    .J(High), .clk(CLK_out), .K(High), .Q(Q0), .preset(Present), .reset(Clear));  // open: Qn, en
  J_K_Flip_Flop #(.trigger("falling")) IC7476_2 (
    .J(Q0), .clk(CLK_out), .K(Q0), .Q(Q1), .preset(Present), .reset(Clear));  // open: Qn, en
  and AND (AND_out, Q1, Q0);
  J_K_Flip_Flop #(.trigger("falling")) IC7476_3 (
    .J(AND_out), .clk(CLK_out), .K(AND_out), .Q(Q2), .preset(Present), .reset(Clear));  // open: Qn, en
  Hex_Digit_Display hex_digit_display_1 (.value({Constant, Q2, Q1, Q0}));  // open: dp
endmodule
