// Logisim project Full Adder Using MUX(4-1).circ as structural Verilog: 1 circuit, main circuit main
module main (
  input  A,
  input  constant,
  input  constant_2,
  input  [1:0] B__Cin,
  output Sum,
  output Carry
);

  wire not_1_out;

  not not_1 (not_1_out, A);
  Multiplexer #(.select(2), .enable("false")) multiplexer_1 (
    .in0(A), .in1(not_1_out), .in2(not_1_out), .in3(A), .out(Sum), .sel(B__Cin));
  Multiplexer #(.select(2), .enable("false")) multiplexer_2 (
    .in0(constant), .in1(A), .in2(A), .in3(constant_2), .out(Carry), .sel(B__Cin));
endmodule
